# Fritzing sketch Untitled Sketch (saved by Fritzing 0.9.3b)
breadboards: 1

parts:
  Part1 = Arduino Micro (Rev3)
  KY-5 = Keyes Relay [package=THT]
  LCD1 = LCD screen
  Part2 = KY-013 Analog Temperature Sensor Module [package="Breakout board"]

nets:
  N1: Part1.D2/SDA, LCD1.DB7
  N2: Part1.D3/SCL, LCD1.DB6
  N3: Part1.D4_PWM/A6, LCD1.DB5
  N4: Part1.D5_PWM, LCD1.DB4
  N5: Part1.D6_PWM/A7, LCD1.V0
  N6: Part1.D8_PWM/A8, KY-5.signal
  N7: Part1.D9_PWM/A9, LCD1.LED+
  N8: Part1.D11_PWM, LCD1.E
  N9: Part1.D12_PWM/A11, LCD1.RS
  GND: Part1.GND, KY-5.ground, LCD1.VSS, LCD1.R/W, LCD1.LED-, Part2.-
  5V: Part1.5V, KY-5.power, LCD1.VDD, Part2.Vin
  N10: Part1.A1, Part2.S

custom parts:
  Keyes Relay: The Keyes 5V relay module is suitable for SCM development, home appliance control. It uses a 5V~12V TIL control signal which can control DC / AC signal.
  KY-013 Analog Temperature Sensor Module: KY-013 Analog Temperature Sensor module, measures ambient temperature based on resistance of the thermistor.
